// Logisim project TinyCPU.circ as structural Verilog: 6 circuits, main circuit TinyCPU
module TinyCPU (
  input  CLK,
  output HALTED
);

  wire errorflags_1_ovf_out, memory_1_valid_out;
  wire [15:0] addresspath_1_address, datapath_1_acc_out, fetchdecode_1_pc_out;

  FetchDecode fetchdecode_1 (.PC_OUT(fetchdecode_1_pc_out));  // open: CLK, RESET, PROGRAM_LIMIT, ZERO, NEGATIVE, ERROR, OPERAND, LOAD_CONST, LOAD_ADDRESS, OPCODE, LOAD_ADDRESS_REGISTER, LOAD_ADDRESS_REGISTER_PLUS_OFFSET, ADD_CONST, ADD_ADDRESS, ADD_ADDRESS_REGISTER, ADD_ADDRESS_REGISTER_PLUS_OFFSET, SUB_CONST, SUB_ADDRESS, SUB_ADDRESS_REGISTER, SUB_ADDRESS_REGISTER_PLUS_OFFSET, MUL_CONST, MUL_ADDRESS, MUL_ADDRESS_REGISTER, MUL_ADDRESS_REGISTER_PLUS_OFFSET, DIV_CONST, DIV_ADDRESS, DIV_ADDRESS_REGISTER, DIV_ADDRESS_REGISTER_PLUS_OFFSET, AND_CONST, AND_ADDRESS, AND_ADDRESS_REGISTER, AND_ADDRESS_REGISTER_PLUS_OFFSET, OR_CONST, OR_ADDRESS, OR_ADDRESS_REGISTER, OR_ADDRESS_REGISTER_PLUS_OFFSET, STORE_ADDRESS, STORE_ADDRESS_REGISTER, STORE_ADDRESS_REGISTER_PLUS_OFFSET, LOAD_ADDRESS_REGISTER_CONST, LOAD_ADDRESS_REGISTER_ADDRESS, NOT, JUMP_ADDRESS, JUMP_ZERO, JUMP_NOT_ZERO, JUMP_NEGATIVE, JUMP_ERROR, JUMP_NOT_ERROR, CLEAR_ERROR, INPUT, PRINT, PRINT_ADDRESS, HALT, HALT_ERROR, SET_OVF, SET_DIV0, SET_ADDR, SET_INV, SET_ILL, SET_INPUT
  Datapath datapath_1 (.ACC_OUT(datapath_1_acc_out));  // open: DATA_IN, ACC_LOAD, VALID_IN, CLK, ZERO, NEGATIVE, ACC_VALID_OUT
  AddressPath addresspath_1 (.ADDRESS(addresspath_1_address));  // open: ADDRESS_IN, AR_LOAD, OFFSET, VALID_IN, CLK, ADDRESS_PLUS_OFFSET, OFFSET_CARRY, ADDRESS_VALID
  Memory memory_1 (.VALID_OUT(memory_1_valid_out));  // open: ADDRESS, WRITE_ENABLE, CLK, VALID_IN, DATA_IN, DATA_OUT
  ErrorFlags errorflags_1 (.OVF_OUT(errorflags_1_ovf_out));  // open: CLEAR_ERROR, CLK, SET_OVF, SET_DIV0, SET_ADDR, SET_INV, SET_ILL, SET_INPUT, DIV0_OUT, ADDR_OUT, INV_OUT, ILL_OUT, INPUT_OUT

  // Notes on the sheet:
  //   TinyCPU AP 5: countdown fixture and clock-edge trace boundary
endmodule

module Datapath (
  input  [15:0] DATA_IN,
  input  ACC_LOAD,
  input  VALID_IN,
  input  CLK,
  output [15:0] ACC_OUT,
  output ZERO,
  output NEGATIVE,
  output ACC_VALID_OUT
);

  Register #(.width(16)) ACC (.D(DATA_IN), .en(ACC_LOAD), .clk(CLK), .Q(ACC_OUT));  // open: clr
  Register #(.width(1)) ACC_VALID (.D(VALID_IN), .en(CLK), .clk(ACC_LOAD), .Q(ACC_VALID_OUT));  // open: clr
  Comparator #(.width(16)) ACC_STATUS (.a(ACC_OUT), .b({16{1'b0}}), .eq(ZERO), .lt(NEGATIVE));  // open: gt

  // Notes on the sheet:
  //   Clocked 16-bit accumulator; signed comparator derives ZERO and NEGATIVE
endmodule

module AddressPath (
  input  [15:0] ADDRESS_IN,
  input  AR_LOAD,
  input  [15:0] OFFSET,
  input  VALID_IN,
  input  CLK,
  output [15:0] ADDRESS,
  output [15:0] ADDRESS_PLUS_OFFSET,
  output OFFSET_CARRY,
  output ADDRESS_VALID
);

  Register #(.width(16)) AR (.D(ADDRESS_IN), .en(AR_LOAD), .clk(CLK), .Q(ADDRESS));  // open: clr
  Register #(.width(1)) AR_VALID (.D(VALID_IN), .en(AR_LOAD), .clk(CLK), .Q(ADDRESS_VALID));  // open: clr
  Adder #(.width(16)) OFFSET_ADDER (
    .a(ADDRESS), .b(OFFSET), .out(ADDRESS_PLUS_OFFSET), .cout(OFFSET_CARRY));  // open: cin

  // Notes on the sheet:
  //   Clocked 12-bit address register with combinational offset addition
endmodule

module Memory (
  input  [15:0] ADDRESS,
  input  WRITE_ENABLE,
  input  CLK,
  input  VALID_IN,
  input  [15:0] DATA_IN,
  output VALID_OUT,
  output [15:0] DATA_OUT
);

  RAM #(.addrWidth(12), .dataWidth(1)) VALID_RAM (
    .addr(ADDRESS[11:0]), .we(WRITE_ENABLE), .oe(1'b1), .clk(CLK), .din(VALID_IN), .dout(VALID_OUT));
  RAM #(.addrWidth(12), .dataWidth(16)) DATA_RAM (
    .addr(ADDRESS[11:0]), .we(WRITE_ENABLE), .oe(1'b1), .clk(CLK), .din(DATA_IN), .dout(DATA_OUT));

  // Notes on the sheet:
  //   4096-word value/valid memory with shared address, write-enable, and clock
endmodule

module ErrorFlags (
  input  CLEAR_ERROR,
  input  CLK,
  input  SET_OVF,
  input  SET_DIV0,
  input  SET_ADDR,
  input  SET_INV,
  input  SET_ILL,
  input  SET_INPUT,
  output OVF_OUT,
  output DIV0_OUT,
  output ADDR_OUT,
  output INV_OUT,
  output ILL_OUT,
  output INPUT_OUT
);

  wire HOLD_ADDR_out, HOLD_DIV0_out, HOLD_ILL_out, HOLD_INPUT_out, HOLD_INV_out, HOLD_OVF_out, NEXT_ADDR_out,
       NEXT_DIV0_out, NEXT_ILL_out, NEXT_INPUT_out, NEXT_INV_out, NEXT_OVF_out, NOT_CLEAR_ERROR_out;

  not NOT_CLEAR_ERROR (NOT_CLEAR_ERROR_out, CLEAR_ERROR);
  and HOLD_OVF (HOLD_OVF_out, OVF_OUT, NOT_CLEAR_ERROR_out);
  and HOLD_DIV0 (HOLD_DIV0_out, DIV0_OUT, NOT_CLEAR_ERROR_out);
  and HOLD_ADDR (HOLD_ADDR_out, ADDR_OUT, NOT_CLEAR_ERROR_out);
  and HOLD_INV (HOLD_INV_out, INV_OUT, NOT_CLEAR_ERROR_out);
  and HOLD_ILL (HOLD_ILL_out, ILL_OUT, NOT_CLEAR_ERROR_out);
  and HOLD_INPUT (HOLD_INPUT_out, INPUT_OUT, NOT_CLEAR_ERROR_out);
  or NEXT_OVF (NEXT_OVF_out, SET_OVF, HOLD_OVF_out);
  or NEXT_DIV0 (NEXT_DIV0_out, SET_DIV0, HOLD_DIV0_out);
  or NEXT_ADDR (NEXT_ADDR_out, SET_ADDR, HOLD_ADDR_out);
  or NEXT_INV (NEXT_INV_out, SET_INV, HOLD_INV_out);
  or NEXT_ILL (NEXT_ILL_out, SET_ILL, HOLD_ILL_out);
  or NEXT_INPUT (NEXT_INPUT_out, SET_INPUT, HOLD_INPUT_out);
  Register #(.width(1)) OVF (.D(NEXT_OVF_out), .en(1'b1), .clk(CLK), .Q(OVF_OUT));  // open: clr
  Register #(.width(1)) DIV0 (.D(NEXT_DIV0_out), .en(1'b1), .clk(CLK), .Q(DIV0_OUT));  // open: clr
  Register #(.width(1)) ADDR (.D(NEXT_ADDR_out), .en(1'b1), .clk(CLK), .Q(ADDR_OUT));  // open: clr
  Register #(.width(1)) INV (.D(NEXT_INV_out), .en(1'b1), .clk(CLK), .Q(INV_OUT));  // open: clr
  Register #(.width(1)) ILL (.D(NEXT_ILL_out), .en(1'b1), .clk(CLK), .Q(ILL_OUT));  // open: clr
  Register #(.width(1)) INPUT (.D(NEXT_INPUT_out), .en(1'b1), .clk(CLK), .Q(INPUT_OUT));  // open: clr

  // Other names for the same wires on the sheet: CURRENT_ADDR = ADDR_OUT; CURRENT_DIV0 = DIV0_OUT;
  //   CURRENT_ILL = ILL_OUT; CURRENT_INPUT = INPUT_OUT; CURRENT_INV = INV_OUT; CURRENT_OVF = OVF_OUT

  // Notes on the sheet:
  //   Set-dominant sticky flags: SET OR (current AND NOT CLEAR_ERROR)
endmodule

module FetchDecode (
  input  CLK,
  input  RESET,
  input  [15:0] PROGRAM_LIMIT,
  input  ZERO,
  input  NEGATIVE,
  input  ERROR,
  output [15:0] PC_OUT,
  output [15:0] OPERAND,
  output LOAD_CONST,
  output LOAD_ADDRESS,
  output [5:0] OPCODE,
  output LOAD_ADDRESS_REGISTER,
  output LOAD_ADDRESS_REGISTER_PLUS_OFFSET,
  output ADD_CONST,
  output ADD_ADDRESS,
  output ADD_ADDRESS_REGISTER,
  output ADD_ADDRESS_REGISTER_PLUS_OFFSET,
  output SUB_CONST,
  output SUB_ADDRESS,
  output SUB_ADDRESS_REGISTER,
  output SUB_ADDRESS_REGISTER_PLUS_OFFSET,
  output MUL_CONST,
  output MUL_ADDRESS,
  output MUL_ADDRESS_REGISTER,
  output MUL_ADDRESS_REGISTER_PLUS_OFFSET,
  output DIV_CONST,
  output DIV_ADDRESS,
  output DIV_ADDRESS_REGISTER,
  output DIV_ADDRESS_REGISTER_PLUS_OFFSET,
  output AND_CONST,
  output AND_ADDRESS,
  output AND_ADDRESS_REGISTER,
  output AND_ADDRESS_REGISTER_PLUS_OFFSET,
  output OR_CONST,
  output OR_ADDRESS,
  output OR_ADDRESS_REGISTER,
  output OR_ADDRESS_REGISTER_PLUS_OFFSET,
  output STORE_ADDRESS,
  output STORE_ADDRESS_REGISTER,
  output STORE_ADDRESS_REGISTER_PLUS_OFFSET,
  output LOAD_ADDRESS_REGISTER_CONST,
  output LOAD_ADDRESS_REGISTER_ADDRESS,
  output NOT,
  output JUMP_ADDRESS,
  output JUMP_ZERO,
  output JUMP_NOT_ZERO,
  output JUMP_NEGATIVE,
  output JUMP_ERROR,
  output JUMP_NOT_ERROR,
  output CLEAR_ERROR,
  output INPUT,
  output PRINT,
  output PRINT_ADDRESS,
  output HALT,
  output HALT_ERROR,
  output SET_OVF,
  output SET_DIV0,
  output SET_ADDR,
  output SET_INV,
  output SET_ILL,
  output SET_INPUT
);

  wire undriven_2, undriven_3;
  wire [10:5] undriven;
  wire [15:0] PC_p3, PC_SOURCE_out;

  // Register #(.width(16)) PC: pin names not known; wires that end beside it: CLK, RESET, PC_p3
  ROM #(.addrWidth(12), .dataWidth(22)) INSTRUCTION_ROM (.addr(PC_p3[11:0]));  // open: data
  // Comparator #(.width(16)) PC_RANGE: pin names not known; wires that end beside it: PROGRAM_LIMIT
  Adder #(.width(16)) PC_INCREMENT (.out(PC_OUT));  // open: a, b, cin, cout
  Decoder #(.select(6)) ISA_DECODER ();  // open: out0, out1, out2, out3, out4, out5, out6, out7, out8, out9, out10, out11, out12, out13, out14, out15, out16, out17, out18, out19, out20, out21, out22, out23, out24, out25, out26, out27, out28, out29, out30, out31, out32, out33, out34, out35, out36, out37, out38, out39, out40, out41, out42, out43, out44, out45, out46, out47, out48, out49, out50, out51, out52, out53, out54, out55, out56, out57, out58, out59, out60, out61, out62, out63, sel, en
  Multiplexer #(.width(16)) PC_SOURCE (.out(PC_SOURCE_out));  // open: in0, in1, sel
  buf JNZ_TAKEN (JUMP_NOT_ZERO, undriven_2);  // AND_Gate
  buf ERROR_HALT (HALT_ERROR, undriven_3);  // OR_Gate
  // Pins of 16 and 22 bits meet at {undriven, OPERAND}

  // Notes on the sheet:
  //   contents of INSTRUCTION_ROM (hex, n*v repeats v):
  //   00ffff 1c0065 000003 1c0064 2a0000 050065 1c0064 240004 2c0000
endmodule
