// Logisim project TinyCPU-AddressPath.circ as structural Verilog: 1 circuit, main circuit AddressPath
module AddressPath (
  input  [11:0] ADDRESS_IN,
  input  [11:0] OFFSET,
  input  AR_LOAD,
  input  VALID_IN,
  input  CLK,
  output [11:0] ADDRESS,
  output ADDRESS_VALID,
  output [11:0] ADDRESS_PLUS_OFFSET,
  output OFFSET_CARRY
);

  Register #(.width(12)) AR (.D(ADDRESS_IN), .Q(ADDRESS), .clk(AR_LOAD));  // open: en, clr
  Register #(.width(1)) AR_VALID (.D(VALID_IN), .Q(ADDRESS_VALID), .clk(AR_LOAD));  // open: en, clr
  // Adder #(.width(12)) OFFSET_ADDER: pin names not known; wires that end beside it: ADDRESS, OFFSET, ADDRESS_PLUS_OFFSET, OFFSET_CARRY

  // Notes on the sheet:
  //   Clocked 12-bit address register with combinational offset addition
endmodule
